// Logisim project fib15.circ as structural Verilog: 1 circuit, main circuit main
module main (
  output [15:0] out_1
);

  wire clock_1_out, comparator_1_lt, comparator_2_eq;
  wire [7:0] counter_1_q;
  wire [15:0] adder_1_out, F_n_1_q, F_n_2_q, multiplexer_1_out;

  Clock clock_1 (.out(clock_1_out));
  Counter counter_1 (.Q(counter_1_q), .clk(clock_1_out));  // open: load, D, count, carry, clr
  Register #(.width(16)) F_n_1 (
    .D(multiplexer_1_out), .en(comparator_1_lt), .Q(F_n_1_q), .clk(clock_1_out));  // open: clr
  Register #(.width(16)) F_n_2 (.D(F_n_1_q), .en(comparator_1_lt), .Q(F_n_2_q), .clk(clock_1_out));  // open: clr
  Comparator comparator_1 (.a(counter_1_q), .b(8'h10), .lt(comparator_1_lt));  // open: gt, eq
  Multiplexer #(.width(16), .enable("false")) multiplexer_1 (
    .in0(adder_1_out), .in1(16'h1), .out(multiplexer_1_out), .sel(comparator_2_eq));
  // Probe on F_n_2_q
  Adder #(.width(16)) adder_1 (.a(F_n_1_q), .b(F_n_2_q), .out(adder_1_out));  // open: cin, cout
  Multiplexer #(.width(16), .enable("false")) multiplexer_2 (
    .in0(F_n_2_q), .in1(16'h1), .out(out_1), .sel(comparator_2_eq));
  Comparator comparator_2 (.a({8{1'b0}}), .b(counter_1_q), .eq(comparator_2_eq));  // open: gt, lt
endmodule
