// Logisim project rotr.circ as structural Verilog: 5 circuits, main circuit main
module main (
  input  [15:0] in_1,
  input  [3:0] in_2,
  output [15:0] out_3
);

  wire [15:0] sub1_1_out_3, sub2_1_out_3, sub4_1_out_3;

  sub1 sub1_1 (.in_1(in_1), .in_2(in_2[0]), .out_3(sub1_1_out_3));
  sub2 sub2_1 (.in_1(sub1_1_out_3), .in_2(in_2[1]), .out_3(sub2_1_out_3));
  sub4 sub4_1 (.in_1(sub2_1_out_3), .in_2(in_2[2]), .out_3(sub4_1_out_3));
  sub8 sub8_1 (.in_1(sub4_1_out_3), .in_2(in_2[3]), .out_3(out_3));
endmodule

module sub1 (
  input  [15:0] in_1,
  input  in_2,
  output [15:0] out_3
);

  Multiplexer #(.width(16), .enable("false")) multiplexer_1 (
    .in0(in_1), .in1({in_1[0], in_1[15:1]}), .out(out_3), .sel(in_2));
endmodule

module sub2 (
  input  [15:0] in_1,
  input  in_2,
  output [15:0] out_3
);

  wire [15:0] sub1_1_out_3;

  sub1 sub1_1 (.in_1(in_1), .in_2(in_2), .out_3(sub1_1_out_3));
  sub1 sub1_2 (.in_1(sub1_1_out_3), .in_2(in_2), .out_3(out_3));
endmodule

module sub4 (
  input  [15:0] in_1,
  input  in_2,
  output [15:0] out_3
);

  wire [15:0] sub2_1_out_3;

  sub2 sub2_1 (.in_1(in_1), .in_2(in_2), .out_3(sub2_1_out_3));
  sub2 sub2_2 (.in_1(sub2_1_out_3), .in_2(in_2), .out_3(out_3));
endmodule

module sub8 (
  input  [15:0] in_1,
  input  in_2,
  output [15:0] out_3
);

  wire [15:0] sub4_1_out_3;

  sub4 sub4_1 (.in_1(in_1), .in_2(in_2), .out_3(sub4_1_out_3));
  sub4 sub4_2 (.in_1(sub4_1_out_3), .in_2(in_2), .out_3(out_3));
endmodule
