// Logisim project logism.circ as structural Verilog: 7 circuits, main circuit main
module main (
  input  in_1,
  input  in_2,
  output out_3,
  output [7:0] out_4,
  output [7:0] out_5
);

  NAND nand_1 (.in_1(in_1), .in_2(in_2), .out_3(out_3));
  AddMachine addmachine_1 (.out_1(out_4), .out_2(out_5));
endmodule

module NAND (
  input  in_1,
  input  in_2,
  output out_3
);

  wire not_1_out;

  not not_1 (not_1_out, in_2);
  and and_1 (out_3, in_1, in_1, not_1_out);
endmodule

module NOR (
  input  in_1,
  input  in_2,
  output out_3
);

  wire not_1_out;

  not not_1 (not_1_out, in_2);
  or or_1 (out_3, in_1, not_1_out);
endmodule

module XOR (
  input  in_1,
  input  in_2,
  output out_3
);

  wire and_1_out, and_2_out, not_1_out, not_2_out;

  not not_1 (not_1_out, in_2);
  and and_1 (and_1_out, not_2_out, in_2);
  not not_2 (not_2_out, in_1);
  and and_2 (and_2_out, in_1, not_1_out);
  or or_1 (out_3, and_1_out, and_2_out);
endmodule

module _2_to_1_MUK (
  input  in_1,
  input  in_2,
  input  in_3,
  output out_4
);

  wire and_1_out, and_2_out, not_1_out;

  not not_1 (not_1_out, in_2);
  and and_1 (and_1_out, in_1, not_1_out);
  and and_2 (and_2_out, in_2, in_3);
  or or_1 (out_4, and_1_out, and_2_out);
endmodule

module _4_to_1 (
  input  in_1,
  input  in_2,
  input  in_3,
  input  in_4,
  input  in_5,
  input  in_6,
  output out_7
);

  wire n2_to_1_muk_1_out_4, n2_to_1_muk_2_out_4;

  _2_to_1_MUK u_2_to_1_muk_1 (.in_1(in_1), .in_2(in_2), .in_3(in_3), .out_4(n2_to_1_muk_1_out_4));
  _2_to_1_MUK u_2_to_1_muk_2 (.in_1(in_4), .in_2(in_5), .in_3(in_3), .out_4(n2_to_1_muk_2_out_4));
  _2_to_1_MUK u_2_to_1_muk_3 (.in_1(n2_to_1_muk_1_out_4), .in_2(n2_to_1_muk_2_out_4), .in_3(in_6), .out_4(out_7));
endmodule

module AddMachine (
  output [7:0] out_1,
  output [7:0] out_2
);

  wire clock_1_out;

  Adder adder_1 (.a(8'h1), .b(out_2), .out(out_1));  // open: cin, cout
  Register register_1 (.D(out_1), .Q(out_2), .clk(clock_1_out));  // open: en, clr
  Clock clock_1 (.out(clock_1_out));
endmodule
