// Logisim project ALU.circ as structural Verilog: 4 circuits, main circuit Ida ALU
// ALU
module Ida_ALU (
  input  [23:0] ALU_Source_1,
  input  [23:0] ALU_Source_2,
  input  [3:0] Operation,
  output [23:0] ALU_Result
);

  wire [4:0] under24_1_out_2;
  wire [23:0] add, \and , \or , rotl, rotr, sll, slt_s, slt_u, sra, srl, sub, \xor ;

  // Probe on ALU_Source_1
  // Probe on ALU_Source_2
  // Probe on Operation
  // Probe on ALU_Result
  Under24 under24_1 (.in_1(ALU_Source_1[4:0]), .out_2(under24_1_out_2));
  Shifter #(.width(24)) shifter_1 (.in(ALU_Source_2), .\dist (under24_1_out_2), .out(sll));
  Shifter #(.width(24), .shift("lr")) shifter_2 (.in(ALU_Source_2), .\dist (under24_1_out_2), .out(srl));
  Shifter #(.width(24), .shift("ar")) shifter_3 (.in(ALU_Source_2), .\dist (under24_1_out_2), .out(sra));
  Shifter #(.width(24), .shift("rl")) shifter_4 (.in(ALU_Source_2), .\dist (under24_1_out_2), .out(rotr));
  Shifter #(.width(24), .shift("rr")) shifter_5 (.in(ALU_Source_2), .\dist (under24_1_out_2), .out(rotl));
  Adder #(.width(24)) adder_1 (.a(ALU_Source_2), .b(ALU_Source_1), .out(add));  // open: cin, cout
  Subtractor #(.width(24)) subtractor_1 (.a(ALU_Source_2), .b(ALU_Source_1), .out(sub));  // open: bin, bout
  compare_signed compare_signed_1 (.in_1(ALU_Source_2), .in_2(ALU_Source_1), .out_3(slt_s));
  compare compare_1 (.in_1(ALU_Source_2), .in_2(ALU_Source_1), .out_3(slt_u));
  assign \and  = ALU_Source_2 & ALU_Source_2 & ALU_Source_1;  // AND_Gate and_1, 24 bits wide
  assign \or  = ALU_Source_2 | ALU_Source_1;  // OR_Gate or_1, 24 bits wide
  assign \xor  = ALU_Source_2 ^ ALU_Source_1;  // XOR_Gate xor_1, 24 bits wide
  Multiplexer #(.select(4), .width(24)) multiplexer_1 (
    .in0(sll), .in1(srl), .in2(sra), .in3(rotl), .in4(rotr), .in5(\and ), .in6(\or ), .in7(\xor ), .in8(add),
    .in9(sub), .in10(add), .in11(add), .in12(slt_s), .in13(slt_u), .in14({24{1'b0}}), .in15({24{1'b0}}),
    .out(ALU_Result), .sel(Operation));  // open: en

  // Other names for the same wires on the sheet: op[3:0] = Operation; result[23:0] = ALU_Result;
  //   s1[23:0] = ALU_Source_1; s2[23:0] = ALU_Source_2

  // Notes on the sheet:
  //   INPUTS
  //   INPUT PROBES
  //   DO NOT MOVE/ADD/CHANGE ANY INPUT OR OUTPUT PINS!
  //   OUTPUT PROBES
  //   OUTPUT
endmodule

module Under24 (
  input  [4:0] in_1,
  output [4:0] out_2
);

  wire comparator_1_gt;

  Comparator #(.width(5)) comparator_1 (.a(in_1), .b(5'b11000), .gt(comparator_1_gt));  // open: eq, lt
  Multiplexer #(.width(5)) multiplexer_1 (.in0({5{1'b0}}), .in1(in_1), .out(out_2), .sel(comparator_1_gt));  // open: en
endmodule

module compare (
  input  [23:0] in_1,
  input  [23:0] in_2,
  output [23:0] out_3
);

  wire comparator_1_gt, comparator_3_eq, comparator_5_lt;
  wire [6:1] not_1_out;

  Comparator #(.width(24), .mode("unsigned")) comparator_1 (.a(in_1), .b(in_2), .gt(comparator_1_gt));  // open: eq, lt
  Comparator #(.width(24), .mode("unsigned")) comparator_2 (.a(in_1), .b(in_2), .gt(not_1_out[2]));  // open: eq, lt
  Comparator #(.width(24), .mode("unsigned")) comparator_3 (.a(in_1), .b(in_2), .eq(comparator_3_eq));  // open: gt, lt
  Comparator #(.width(24), .mode("unsigned")) comparator_4 (.a(in_1), .b(in_2), .eq(not_1_out[4]));  // open: gt, lt
  Comparator #(.width(24), .mode("unsigned")) comparator_5 (.a(in_1), .b(in_2), .lt(comparator_5_lt));  // open: gt, eq
  Comparator #(.width(24), .mode("unsigned")) comparator_6 (.a(in_1), .b(in_2), .lt(not_1_out[6]));  // open: gt, eq
  not not_1 (not_1_out[1], comparator_1_gt);
  not not_2 (not_1_out[3], comparator_3_eq);
  not not_3 (not_1_out[5], comparator_5_lt);
  assign out_3 = {{16{1'b0}}, {1'b1, not_1_out, 1'b0}};  // Bit_Extender bit_extender_1

  // Other names for the same wires on the sheet: arg1[23:0] = in_1; arg2[23:0] = in_2
endmodule

module compare_signed (
  input  [23:0] in_1,
  input  [23:0] in_2,
  output [23:0] out_3
);

  wire comparator_1_gt, comparator_3_eq, comparator_5_lt;
  wire [6:1] not_1_out;

  Comparator #(.width(24)) comparator_1 (.a(in_1), .b(in_2), .gt(comparator_1_gt));  // open: eq, lt
  Comparator #(.width(24)) comparator_2 (.a(in_1), .b(in_2), .gt(not_1_out[2]));  // open: eq, lt
  Comparator #(.width(24)) comparator_3 (.a(in_1), .b(in_2), .eq(comparator_3_eq));  // open: gt, lt
  Comparator #(.width(24)) comparator_4 (.a(in_1), .b(in_2), .eq(not_1_out[4]));  // open: gt, lt
  Comparator #(.width(24)) comparator_5 (.a(in_1), .b(in_2), .lt(comparator_5_lt));  // open: gt, eq
  Comparator #(.width(24)) comparator_6 (.a(in_1), .b(in_2), .lt(not_1_out[6]));  // open: gt, eq
  not not_1 (not_1_out[1], comparator_1_gt);
  not not_2 (not_1_out[3], comparator_3_eq);
  not not_3 (not_1_out[5], comparator_5_lt);
  assign out_3 = {{16{1'b0}}, {1'b1, not_1_out, 1'b0}};  // Bit_Extender bit_extender_1

  // Other names for the same wires on the sheet: arg1[23:0] = in_1; arg2[23:0] = in_2
endmodule
