// Logisim project CPU.circ as structural Verilog: 4 circuits, main circuit Ida CPU
// CPU
module Ida_CPU (
  input  [31:0] Instruction,
  input  Clock,
  output [23:0] Mem_Data,
  output [23:0] Mem_Address,
  output Mem_Write,
  output [23:0] Next_PC,
  output [23:0] r00,
  output [23:0] r01,
  output [23:0] r02,
  output [23:0] r03,
  output [23:0] r04,
  output [23:0] r05,
  output [23:0] r06,
  output [23:0] r07,
  output [23:0] r08,
  output [23:0] r09,
  output [23:0] r10,
  output [23:0] r11,
  output [23:0] r12,
  output [23:0] r13,
  output [23:0] r14,
  output [23:0] r15
);

  wire checkcomp_1_out_3, checkcomp_2_out_3, checkcomp_3_out_3, checkcomp_4_out_3, comparator_1_eq,
       comparator_2_eq, comparator_4_eq, comparator_5_eq, comparator_6_eq, comparator_7_eq, comparator_8_eq,
       comparator_9_lt, comparator_10_eq, comparator_11_eq, comparator_12_eq, imm_t, jump, link, memToReg,
       or_1_out, or_2_out, or_3_out, or_4_out, or_5_out, or_6_out, regWrite;
  wire [2:0] cq;
  wire [3:0] multiplexer_3_out, op, reg1, reg2, reg3;
  wire [23:0] adder_1_out, cr, ida_register_file_1_reg_1_value, ida_register_file_1_reg_2_value, imm,
       multiplexer_2_out, multiplexer_4_out, multiplexer_6_out, pipeline, ram_1_data, RI_value, writeVal;
  wire [31:0] multiplexer_1_out;

  // Probe on Instruction
  // Probe on Clock
  // Probe on r00
  // Probe on r01
  // Probe on r02
  // Probe on r03
  // Probe on r04
  // Probe on r05
  // Probe on r06
  // Probe on r07
  // Probe on Mem_Data
  // Probe on Mem_Address
  // Probe on Mem_Write
  // Probe on Next_PC
  // Probe on r08
  // Probe on r09
  // Probe on r10
  // Probe on r11
  // Probe on r12
  // Probe on r13
  // Probe on r14
  // Probe on r15
  checkComp checkcomp_1 (.cq(cq), .cr(cr), .out_3(checkcomp_1_out_3));
  Comparator #(.width(3)) comparator_1 (.a(cq), .b(3'b111), .eq(comparator_1_eq));  // open: gt, lt
  Comparator #(.width(4)) comparator_2 (.a(op), .b(4'b1111), .eq(comparator_2_eq));  // open: gt, lt
  Comparator #(.width(4), .mode("unsigned")) comparator_3 (.a(op), .b(4'b1110), .eq(link));  // open: gt, lt
  or or_1 (or_1_out, checkcomp_1_out_3, comparator_1_eq);
  // Probe on op
  // Probe on imm_t
  // Probe on reg1
  setRegisters setregisters_1 (.in_1({op, cq, imm_t, pipeline}), .reg1(reg1), .reg2(reg2), .reg3(reg3));
  // Probe on reg2
  // Probe on reg3
  setRegistersImm setregistersimm_1 (.in_1({op, cq, imm_t, pipeline}), .imm(imm));
  // Probe on imm
  Adder #(.width(24)) adder_1 (.a(Next_PC), .b(24'h1), .out(adder_1_out));  // open: cin, cout
  and and_1 (jump, or_1_out, comparator_2_eq);
  Multiplexer #(.width(32), .enable("false")) multiplexer_1 (
    .in0(Instruction), .in1({32{1'b0}}), .out(multiplexer_1_out), .sel(jump));
  Multiplexer #(.width(24), .enable("false")) multiplexer_2 (
    .in0(adder_1_out), .in1(RI_value), .out(multiplexer_2_out), .sel(jump));
  Register #(.width(32)) register_1 (
    .D(multiplexer_1_out), .Q({op, cq, imm_t, pipeline}), .clk(Clock));  // open: en, clr
  Multiplexer #(.width(4), .enable("false")) multiplexer_3 (
    .in0(reg3), .in1(4'b0010), .out(multiplexer_3_out), .sel(link));
  Multiplexer #(.width(24), .enable("false")) multiplexer_4 (
    .in0(writeVal), .in1(RI_value), .out(multiplexer_4_out), .sel(link));
  Register #(.width(24)) register_2 (.D(multiplexer_2_out), .Q(Next_PC), .clk(Clock));  // open: en, clr
  // Probe on regWrite
  Ida_Register_File ida_register_file_1 (
    .Read_Reg_1(reg1), .Read_Reg_2(reg2), .Write_Reg(multiplexer_3_out), .Write_Value(multiplexer_4_out),
    .Reg_1_Value(ida_register_file_1_reg_1_value), .Reg_2_Value(ida_register_file_1_reg_2_value),
    .Reg_Write(regWrite), .Clock(Clock), .r00(r00), .r01(r01), .r02(r02), .r03(r03), .r04(r04), .r05(r05),
    .r06(r06), .r07(r07), .r08(r08), .r09(r09), .r10(r10), .r11(r11), .r12(r12), .r13(r13), .r14(r14),
    .r15(r15), .Reg_3_Value(Mem_Data));
  checkComp checkcomp_2 (.cq(cq), .cr(cr), .out_3(checkcomp_2_out_3));
  Comparator #(.width(3)) comparator_4 (.a(cq), .b(3'b111), .eq(comparator_4_eq));  // open: gt, lt
  Comparator #(.width(4)) comparator_5 (.a(op), .b(4'b1010), .eq(comparator_5_eq));  // open: gt, lt
  Comparator #(.width(4), .mode("unsigned")) comparator_6 (.a(op), .b(4'b1100), .eq(comparator_6_eq));  // open: gt, lt
  or or_2 (or_2_out, checkcomp_2_out_3, comparator_4_eq);
  Multiplexer #(.width(24), .enable("false")) multiplexer_5 (
    .in0(ida_register_file_1_reg_1_value), .in1(imm), .out(RI_value), .sel(imm_t));
  // Probe on ida_register_file_1_reg_2_value
  Comparator #(.width(4), .mode("unsigned")) comparator_7 (.a(op), .b(4'b1101), .eq(comparator_7_eq));  // open: gt, lt
  or or_3 (or_3_out, comparator_6_eq, comparator_7_eq);
  Multiplexer #(.width(24), .enable("false")) multiplexer_6 (
    .in1(writeVal), .out(multiplexer_6_out), .sel(or_3_out));  // open: in0
  and and_2 (memToReg, or_2_out, comparator_5_eq);
  Ida_ALU ida_alu_1 (
    .ALU_Source_1(RI_value), .ALU_Source_2(ida_register_file_1_reg_2_value), .Operation(op),
    .ALU_Result(Mem_Address));
  // Probe on cr
  Register #(.width(24)) register_3 (.D(multiplexer_6_out), .Q(cr), .clk(Clock));  // open: en, clr
  // Probe on Mem_Address
  checkComp checkcomp_3 (.cq(cq), .cr(cr), .out_3(checkcomp_3_out_3));
  Comparator #(.width(3)) comparator_8 (.a(cq), .b(3'b111), .eq(comparator_8_eq));  // open: gt, lt
  Comparator #(.width(4), .mode("unsigned")) comparator_9 (.a(op), .b(4'b1011), .lt(comparator_9_lt));  // open: gt, eq
  Comparator #(.width(4), .mode("unsigned")) comparator_10 (
    .a(op), .b(4'b1110), .eq(comparator_10_eq));  // open: gt, lt
  checkComp checkcomp_4 (.cq(cq), .cr(cr), .out_3(checkcomp_4_out_3));
  Comparator #(.width(3)) comparator_11 (.a(cq), .b(3'b111), .eq(comparator_11_eq));  // open: gt, lt
  Comparator #(.width(4)) comparator_12 (.a(op), .b(4'b1011), .eq(comparator_12_eq));  // open: gt, lt
  or or_4 (or_4_out, checkcomp_3_out_3, comparator_8_eq);
  or or_5 (or_5_out, checkcomp_4_out_3, comparator_11_eq);
  RAM #(.addrWidth(24), .dataWidth(24), .bus("separate")) ram_1 (
    .addr(Mem_Address), .din(Mem_Data), .data(ram_1_data), .str(Mem_Write), .clk(Clock), .ld(memToReg));  // open: sel, clr
  and and_3 (regWrite, or_4_out, or_6_out);
  or or_6 (or_6_out, comparator_9_lt, comparator_10_eq);
  and and_4 (Mem_Write, or_5_out, comparator_12_eq);
  // Probe on memToReg
  Multiplexer #(.width(24), .enable("false")) multiplexer_7 (
    .in0(Mem_Address), .in1(ram_1_data), .out(writeVal), .sel(memToReg));

  // Other names for the same wires on the sheet: clk = Clock; inst[31:0] = Instruction; memAddr[23:0] = Mem_Address;
  //   memData[23:0] = Mem_Data; memWrite = Mem_Write; nextPC[23:0] = Next_PC; pipeline[31:24] = {op, cq, imm_t}

  // Notes on the sheet:
  //   INPUTS
  //   INPUT PROBES
  //   OUTPUT PROBES
  //   OUTPUTS
  //   DO NOT MOVE/ADD/CHANGE ANY INPUT OR OUTPUT PINS!
endmodule

module setRegisters (
  input  [31:0] in_1,
  output [3:0] reg1,
  output [3:0] reg2,
  output [3:0] reg3
);

  wire [1:0] op_code;

  // Probe on in_1[31:28]
  // Probe on in_1[31:28]
  Comparator #(.width(4), .mode("unsigned")) comparator_1 (
    .a(in_1[31:28]), .b(4'b1101), .gt(op_code[1]));  // open: eq, lt
  // Probe on 4'b1101
  Comparator #(.width(4), .mode("unsigned")) comparator_2 (
    .a(in_1[31:28]), .b(4'b1011), .gt(op_code[0]));  // open: eq, lt
  Multiplexer #(.select(2), .width(4), .enable("false")) multiplexer_1 (
    .in0(in_1[19:16]), .in1(in_1[23:20]), .in2(4'b0000), .in3(4'b0000), .out(reg2), .sel(op_code));
  // Probe on reg2
  // Probe on op_code
  Multiplexer #(.select(2), .width(4), .enable("false")) multiplexer_2 (
    .in0(in_1[23:20]), .in1(4'b0000), .in2(4'b0000), .in3(4'b0000), .out(reg3), .sel(op_code));

  assign reg1 = in_1[3:0];

  // Other names for the same wires on the sheet: inst[31:0] = in_1; imm = in_1[24]; op[3:0] = in_1[31:28]
endmodule

module setRegistersImm (
  input  [31:0] in_1,
  output [23:0] imm
);

  wire [1:0] op_code;
  wire [23:0] bit_extender_1_out, bit_extender_2_out;

  Comparator #(.width(4), .mode("unsigned")) comparator_1 (
    .a(in_1[31:28]), .b(4'b1101), .gt(op_code[1]));  // open: eq, lt
  Comparator #(.width(4), .mode("unsigned")) comparator_2 (
    .a(in_1[31:28]), .b(4'b1011), .gt(op_code[0]));  // open: eq, lt
  // Probe on in_1[31:28]
  // Probe on op_code
  assign bit_extender_1_out = {{8{in_1[15]}}, in_1[15:0]};  // Bit_Extender bit_extender_1
  assign bit_extender_2_out = {{4{in_1[19]}}, in_1[19:0]};  // Bit_Extender bit_extender_2
  Multiplexer #(.select(2), .width(24), .enable("false")) multiplexer_1 (
    .in0(bit_extender_1_out), .in1(bit_extender_2_out), .in2({24{1'b0}}), .in3(in_1[23:0]), .out(imm),
    .sel(op_code));

  // Other names for the same wires on the sheet: inst[31:0] = in_1; imm_t = in_1[24]; op[3:0] = in_1[31:28]
endmodule

module checkComp (
  input  [2:0] cq,
  input  [23:0] cr,
  output out_3
);

  Multiplexer #(.select(3), .enable("false")) multiplexer_1 (
    .in0(cr[0]), .in1(cr[1]), .in2(cr[2]), .in3(cr[3]), .in4(cr[4]), .in5(cr[5]), .in6(cr[6]), .in7(cr[7]),
    .out(out_3), .sel(cq));

  // Other names for the same wires on the sheet: cr_t[7:0] = cr[7:0]
endmodule
