// Logisim project REG.circ as structural Verilog: 1 circuit, main circuit Ida Register File
// Register File
module Ida_Register_File (
  input  [3:0] Read_Reg_1,
  input  [3:0] Read_Reg_2,
  input  [3:0] Write_Reg,
  input  [23:0] Write_Value,
  input  Reg_Write,
  input  Clock,
  output [23:0] Reg_1_Value,
  output [23:0] Reg_2_Value,
  output [23:0] Reg_3_Value,
  output [23:0] r00,
  output [23:0] r01,
  output [23:0] r02,
  output [23:0] r03,
  output [23:0] r04,
  output [23:0] r05,
  output [23:0] r06,
  output [23:0] r07,
  output [23:0] r08,
  output [23:0] r09,
  output [23:0] r10,
  output [23:0] r11,
  output [23:0] r12,
  output [23:0] r13,
  output [23:0] r14,
  output [23:0] r15
);

  wire r00_t, r01_t, r02_t, r03_t, r04_t, r05_t, r06_t, r07_t, r08_t, r09_t, r10_t, r11_t, r12_t, r13_t,
       r14_t, r15_t;

  // Probe on Read_Reg_1
  // Probe on Read_Reg_2
  // Probe on Write_Reg
  // Probe on Write_Value
  // Probe on Reg_Write
  // Probe on Clock
  // Probe on Reg_1_Value
  // Probe on Reg_2_Value
  // Probe on Reg_3_Value
  // Probe on r00
  // Probe on r01
  // Probe on r02
  // Probe on r03
  // Probe on r04
  // Probe on r05
  // Probe on r06
  // Probe on r07
  // Probe on r08
  // Probe on r09
  // Probe on r10
  // Probe on r11
  // Probe on r12
  // Probe on r13
  // Probe on r14
  // Probe on r15
  Demultiplexer #(.select(4)) demultiplexer_1 (
    .out0(r00_t), .out1(r01_t), .out2(r02_t), .out3(r03_t), .out4(r04_t), .out5(r05_t), .out6(r06_t),
    .out7(r07_t), .out8(r08_t), .out9(r09_t), .out10(r10_t), .out11(r11_t), .out12(r12_t), .out13(r13_t),
    .out14(r14_t), .out15(r15_t), .in(Reg_Write), .sel(Write_Reg));  // open: en
  Register #(.width(24)) u_R00 (.D(Write_Value), .en(r00_t), .Q(r00), .clk(Clock));  // open: clr
  Register #(.width(24)) u_R01 (.D(Write_Value), .en(r01_t), .Q(r01), .clk(Clock));  // open: clr
  Register #(.width(24)) u_R02 (.D(Write_Value), .en(r02_t), .Q(r02), .clk(Clock));  // open: clr
  Register #(.width(24)) u_R03 (.D(Write_Value), .en(r03_t), .Q(r03), .clk(Clock));  // open: clr
  Register #(.width(24)) u_R04 (.D(Write_Value), .en(r04_t), .Q(r04), .clk(Clock));  // open: clr
  Register #(.width(24)) u_R05 (.D(Write_Value), .en(r05_t), .Q(r05), .clk(Clock));  // open: clr
  Register #(.width(24)) u_R06 (.D(Write_Value), .en(r06_t), .Q(r06), .clk(Clock));  // open: clr
  Register #(.width(24)) u_R07 (.D(Write_Value), .en(r07_t), .Q(r07), .clk(Clock));  // open: clr
  Register #(.width(24)) u_R08 (.D(Write_Value), .en(r08_t), .Q(r08), .clk(Clock));  // open: clr
  Register #(.width(24)) u_R09 (.D(Write_Value), .en(r09_t), .Q(r09), .clk(Clock));  // open: clr
  Register #(.width(24)) u_R10 (.D(Write_Value), .en(r10_t), .Q(r10), .clk(Clock));  // open: clr
  Register #(.width(24)) u_R11 (.D(Write_Value), .en(r11_t), .Q(r11), .clk(Clock));  // open: clr
  Register #(.width(24)) u_R12 (.D(Write_Value), .en(r12_t), .Q(r12), .clk(Clock));  // open: clr
  Register #(.width(24)) u_R13 (.D(Write_Value), .en(r13_t), .Q(r13), .clk(Clock));  // open: clr
  Register #(.width(24)) u_R14 (.D(Write_Value), .en(r14_t), .Q(r14), .clk(Clock));  // open: clr
  Register #(.width(24)) u_R15 (.D(Write_Value), .en(r15_t), .Q(r15), .clk(Clock));  // open: clr
  Multiplexer #(.select(4), .width(24)) multiplexer_1 (
    .in0(r00), .in1(r01), .in2(r02), .in3(r03), .in4(r04), .in5(r05), .in6(r06), .in7(r07), .in8(r08),
    .in9(r09), .in10(r10), .in11(r11), .in12(r12), .in13(r13), .in14(r14), .in15(r15), .out(Reg_1_Value),
    .sel(Read_Reg_1));  // open: en
  Multiplexer #(.select(4), .width(24)) multiplexer_2 (
    .in0(r00), .in1(r01), .in2(r02), .in3(r03), .in4(r04), .in5(r05), .in6(r06), .in7(r07), .in8(r08),
    .in9(r09), .in10(r10), .in11(r11), .in12(r12), .in13(r13), .in14(r14), .in15(r15), .out(Reg_2_Value),
    .sel(Read_Reg_2));  // open: en
  Multiplexer #(.select(4), .width(24)) multiplexer_3 (
    .in0(r00), .in1(r01), .in2(r02), .in3(r03), .in4(r04), .in5(r05), .in6(r06), .in7(r07), .in8(r08),
    .in9(r09), .in10(r10), .in11(r11), .in12(r12), .in13(r13), .in14(r14), .in15(r15), .out(Reg_3_Value),
    .sel(Write_Reg));  // open: en

  // Other names for the same wires on the sheet: clk = Clock; r_00[23:0] = r00; r_01[23:0] = r01; r_02[23:0] = r02;
  //   r_03[23:0] = r03; r_04[23:0] = r04; r_05[23:0] = r05; r_06[23:0] = r06; r_07[23:0] = r07; r_08[23:0] = r08;
  //   r_09[23:0] = r09; r_10[23:0] = r10; r_11[23:0] = r11; r_12[23:0] = r12; r_13[23:0] = r13; r_14[23:0] = r14;
  //   r_15[23:0] = r15; reg1Read[3:0] = Read_Reg_1; reg1Val[23:0] = Reg_1_Value; reg2Read[3:0] = Read_Reg_2;
  //   reg2Val[23:0] = Reg_2_Value; reg3Val[23:0] = Reg_3_Value; reg3Write[3:0] = Write_Reg; write = Reg_Write;
  //   writeVal[23:0] = Write_Value

  // Notes on the sheet:
  //   INPUT PINS
  //   INPUT PROBES
  //   OUTPUT PROBES
  //   OUTPUT PINS
  //   DO NOT MOVE/ADD/CHANGE ANY INPUT OR OUTPUT PINS!
endmodule
